// Digital circuit 15_condition_yanlis_tel.dig as structural Verilog
module _15_condition_yanlis_tel (
  input  lt,
  input  eq,
  input  gt,
  input  [15:0] X,
  output Y
);

  wire is_neg, is_zero, or2, vana_eq, vana_gt, vana_lt, X___0, X__gt__0;

  Comparator #(.Bits(16), .Signed("true")) comparator_1 (
    .a({{15{1'b0}}, eq}), .b({16{1'b0}}), .eq(is_zero));  // open: gt, lt
  Comparator #(.Bits(16), .Signed("true")) comparator_2 (
    .a({{15{1'b0}}, gt}), .b({16{1'b0}}), .lt(is_neg));  // open: gt, eq
  and and_1 (vana_lt, lt, is_neg);
  and and_2 (vana_eq, eq, is_zero);
  and and_3 (vana_gt, gt, X__gt__0);
  or or_1 (X___0, is_zero, is_neg);
  not not_1 (X__gt__0, X___0);
  or or_2 (or2, vana_lt, vana_eq);
  or or_3 (Y, or2, vana_gt);

  // Other names for the same wires on the sheet: eq_16_bit[0] = eq; gt_16_bit[0] = gt

  // Notes on the sheet:
  //   HATALI (dersin kendi tuzağı): is zero ← eq, is neg ← gt; 1 bit sessizce 16 bite genişletildi
  //   Testi çalıştır: Simulation → Run tests (ya da F8). Tabloyu görmek için Test kutusuna çift tıkla. −3 = 65533 (16 bit).
  //   is zero = (X = 0)
  //   is neg = (X < 0)
endmodule

/* Test case 1 Never+Always:
lt eq gt X Y
0 0 0 5 0
0 0 0 0 0
0 0 0 65533 0
1 1 1 5 1
1 1 1 0 1
1 1 1 65533 1
*/

/* Test case 2 tek izinli:
lt eq gt X Y
1 0 0 5 0
1 0 0 0 0
1 0 0 65533 1
0 1 0 5 0
0 1 0 0 1
0 1 0 65533 0
0 0 1 5 1
0 0 1 0 0
0 0 1 65533 0
*/

/* Test case 3 tam tablo:
lt eq gt X Y
0 0 0 5 0
0 0 0 0 0
0 0 0 65533 0
0 0 1 5 1
0 0 1 0 0
0 0 1 65533 0
0 1 0 5 0
0 1 0 0 1
0 1 0 65533 0
0 1 1 5 1
0 1 1 0 1
0 1 1 65533 0
1 0 0 5 0
1 0 0 0 0
1 0 0 65533 1
1 0 1 5 1
1 0 1 0 0
1 0 1 65533 1
1 1 0 5 0
1 1 0 0 1
1 1 0 65533 1
1 1 1 5 1
1 1 1 0 1
1 1 1 65533 1
*/
